# Fritzing sketch gingerbreadrfid (saved by Fritzing 1.0.6)
breadboards: 1

parts:
  U1 = RFID RC522 SIP - 8 pins [chip_label="RFID RC522" package="SIP (Single Inline) [THT]"]
  Part1 = Arduino Uno (Rev3)
  Mod1 = KY-019 5V Relay Module [package="Breakout board"]
  A1 = uhppote electric strike door lock
  V5 = DC Power [voltage=12V internal_resistance=0.1Ω]

nets:
  N1: U1.SDA, Part1.D10_PWM/SS
  N2: U1.SCK, Part1.D13/SCK
  N3: U1.MOSI, Part1.D11_PWM/MOSI
  N4: U1.MISO, Part1.D12/MISO
  GND: U1.GND, Part1.GND, Mod1.-
  N5: U1.RST, Part1.D9_PWM
  3.3V: U1.VCC, Part1.3V3
  N6: Part1.D3_PWM, Mod1.S
  5V: Part1.5V, Mod1.+
  N7: Mod1.NC, A1.pin2
  N8: Mod1.Common, V5.V+
  N9: A1.pin1, V5.V-

custom parts:
  RFID RC522 SIP - 8 pins: A SIP stand-in part for RFID RC522 . With 8 pins on a 300 mil single inline package (SIP) footprint.
  KY-019 5V Relay Module: KY-019 5V Relay module, used to control AC circuits. (Special thanks to vanepp for fixing the PCB holes and other errors)
  uhppote electric strike door lock: UHPPOTE electric strike door lock.
