# Fritzing sketch gobolight (saved by Fritzing 1.0.5)
breadboards: 1

parts:
  Part1 = Arduino Uno (Rev3)
  Part2 = Ambient Light Sensor (TEMT6000 Breakout Board)
  LED1 = LEDs [package=led-0603]
  LED2 = LED - 5mm [color="Red (633nm)" current=0.030A package="5 mm [THT]"]

nets:
  N1: Part1.A0, Part2.S
  GND: Part1.GND, Part2.GND, LED1.C, LED2.cathode
  N2: Part1.D2, LED2.anode
  N3: Part1.D3_PWM, LED1.A
  5V: Part1.5V, Part2.VCC
