# Fritzing sketch simonsays (saved by Fritzing 1.0.5)
breadboards: 1

parts:
  Part1 = Arduino Uno (Rev3) - ICSP
  LED5 = RGB LED (com. cathode, rgb) [color="Red (633nm)" current=0.030A package="5 mm [THT]"]
  R1 = Resistor [tolerance=±5% resistance=330 package="0805 [SMD]"]
  R2 = Resistor [tolerance=±5% resistance=330 package="0805 [SMD]"]
  R3 = Resistor [tolerance=±5% resistance=330 package="0805 [SMD]"]
  LED6 = RGB LED (com. cathode, rgb) [color="Red (633nm)" current=0.030A package="5 mm [THT]"]
  R4 = Resistor [tolerance=±5% resistance=330 package="0805 [SMD]"]
  R5 = Resistor [tolerance=±5% resistance=330 package="0805 [SMD]"]
  R6 = Resistor [tolerance=±5% resistance=330 package="0805 [SMD]"]
  LED7 = RGB LED (com. cathode, rgb) [color="Red (633nm)" current=0.030A package="5 mm [THT]"]
  R7 = Resistor [tolerance=±5% resistance=330 package="0805 [SMD]"]
  R8 = Resistor [tolerance=±5% resistance=330 package="0805 [SMD]"]
  R9 = Resistor [tolerance=±5% resistance=330 package="0805 [SMD]"]
  LED8 = RGB LED (com. cathode, rgb) [color="Red (633nm)" current=0.030A package="5 mm [THT]"]
  R10 = Resistor [tolerance=±5% resistance=330 package="0805 [SMD]"]
  R11 = Resistor [tolerance=±5% resistance=330 package="0805 [SMD]"]
  R12 = Resistor [tolerance=±5% resistance=330 package="0805 [SMD]"]
  JL012-13-5_1 = JL012-13-5.2 Lever (Limit) Switch SPDT + NO + NC [part_number=JL012-13-5.2]
  Part2 = Arduino Uno (Rev3) - ICSP
  Mod1 = KY-019 5V Relay Module [package="Breakout board"]
  JL012-13-5_2 = JL012-13-5.2 Lever (Limit) Switch SPDT + NO + NC [part_number=JL012-13-5.2]
  JL012-13-5_3 = JL012-13-5.2 Lever (Limit) Switch SPDT + NO + NC [part_number=JL012-13-5.2]
  JL012-13-5_4 = JL012-13-5.2 Lever (Limit) Switch SPDT + NO + NC [part_number=JL012-13-5.2]
  A1 = Raspberry Pi 5
  A2 = uhppote electric strike door lock
  V4 = DC Power [voltage=12V]

nets:
  N1: Part1.ICSP_SCK, Part1.D13/SCK, R3.Pin_0
  GND: Part1.GND, LED5.common_cathode, LED6.common_cathode, LED7.common_cathode, LED8.common_cathode, JL012-13-5_1.C, Part2.GND, Mod1.-, JL012-13-5_2.C, JL012-13-5_3.C, JL012-13-5_4.C
  N2: Part1.D9_PWM, R5.Pin_0
  N3: Part1.D10_PWM/SS, Part2.D10_PWM/SS, A1.GPIO26
  N4: Part1.D2, R11.Pin_0
  N5: Part1.D3_PWM, R10.Pin_0
  N6: Part1.D4, R12.Pin_0
  N7: Part1.D5_PWM, R8.Pin_0
  N8: LED5.red_anode, R3.Pin_1
  N9: LED5.green_anode, R2.Pin_1
  N10: LED5.blue_anode, R1.Pin_1
  N11: LED6.red_anode, R4.Pin_1
  N12: LED6.green_anode, R5.Pin_1
  N13: LED6.blue_anode, R6.Pin_1
  N14: LED7.red_anode, R7.Pin_1
  N15: LED7.green_anode, R9.Pin_1
  N16: LED7.blue_anode, R8.Pin_1
  N17: LED8.red_anode, R12.Pin_1
  N18: LED8.green_anode, R10.Pin_1
  N19: LED8.blue_anode, R11.Pin_1
  N20: JL012-13-5_1.NO, Part2.D2
  N21: Part2.ICSP_MISO, Part2.D12/MISO, Mod1.S
  5V: Part2.5V, Mod1.+
  N22: Part2.D8, JL012-13-5_4.NO
  N23: Part2.D4, JL012-13-5_2.NO
  N24: Part2.D6_PWM, JL012-13-5_3.NO
  N25: Mod1.NC, A2.pin1
  N26: Mod1.Common, V4.V+
  N27: A2.pin2, V4.V-

custom parts:
  JL012-13-5.2 Lever (Limit) Switch SPDT + NO + NC: Micro Switch; Model No.: JL012-13.5-2; Actuator Action: Momentary; Actuator Type: Hinge Lever; Contact Configuration: 1NO, 1NC (SPDT) Temperature -25~65℃；Relative humidity: below 85%; Rate Voltage: 125V AC; Rated Current: 1A.
  KY-019 5V Relay Module: KY-019 5V Relay module, used to control AC circuits. (Special thanks to vanepp for fixing the PCB holes and other errors)
  Raspberry Pi 5: The RPi5, a faster version of the awesome Raspberry Pi4B ARM Board with 40 pin gpio.
  uhppote electric strike door lock: UHPPOTE electric strike door lock.
